# Fritzing sketch Guitar Hack Diagram (saved by Fritzing 1.0.0rc)
circuit board: 8.46667cm x 5.64444cm
breadboards: 1

parts:
  U1 = 74HC4052 [package=dil16]
  U2 = 74HC4052 [package=dil16]
  Part1 = Arduino Pro Micro (Clone)
  OLED1 = OLED 128x64 I2C Monochrome Display GND-VDD
  TRS1 = Audio Jack (TRS) 3.5mm [package="4Ucon 08780 [THT]"]
  R3 = Resistor [tolerance=±5% resistance=220 package="1206 [SMD]"]
  U3 = 74HC4052 [package=dil16]

nets:
  N1: U1.Y, U2.Y, Part1.D7, U3.Y
  N2: U1.INH, Part1.D14
  GND: U1.VEE, U1.GND, U2.VEE, U2.GND, Part1.GND, OLED1.GND, TRS1.Sleeve, U3.VEE, U3.GND
  N3: U1.B, U2.B, Part1.D8, U3.B
  N4: U1.A, U2.A, Part1.D15, U3.A
  N5: U1.X3, U2.X3, Part1.D4, U3.X3
  VCC: U1.VCC, U2.VCC, Part1.VCC, R3.Pin_1, U3.VCC
  N6: U2.INH, Part1.D16
  N7: Part1.TXO, TRS1.Tip
  N8: Part1.D2, OLED1.SDA
  N9: Part1.D3, OLED1.SCK
  N10: Part1.D10, U3.INH
  N11: TRS1.Ring, R3.Pin_0

notes:
  3: Low Blue
  0: Low Green
  1: Low Red
  2: Low Yellow
  5: High Green
  7: High Yellow
  6: High Red
  4: Low Orange
  13: Bridge Up
  15: Right Arrow
  14: Up Arrow
  12: Bridge Down
  11: Neck Up
  8: High Blue
  9: High Orange
  10: Neck Down
  19: Select
  16: Down Arrow
  17: Left Arrow
  18: Start
  Button index 21
  Button index 23
  Button index 22
  20: Menu / Save
  MIDI OUTPUT TRS

custom parts:
  OLED 128x64 I2C Monochrome Display GND-VDD: OLED 128x64 I2C Monochrome Display. Note: there are two variants of this part, this one is the GND VDD SCK SDA variant. The other is VDD GND SCK SDA. Make sure you select the part that matches your module as using the incorrect part will probably destroy your module! In addition the mounting holes are marked on silkscreen but not by default drilled. If you want drilled mounting holes, copy a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
